// Logisim project s-mips.circ as structural Verilog: 10 circuits, main circuit S_MIPS_Board_ef91e4f6
module S_MIPS_Board_ef91e4f6 (
  input  DESHABILITAR_DISPATCHER_e4100c26,
  output halt
);

  wire button_1_out, CLK, CS, d_ff_1_q, LCLR, LoadRAM, LoadRAMOn, LW, R_R_W_3abe9cfd, R_W_ea6840f6,
       ram_dispatcher_8f9b374a_1_finished, RCS, Reset_out, RST, TTY_EN_70a2b517;
  wire [2:0] KDB;
  wire [3:0] LMask, Mask, ram_1_read_time_acdb67b1, ram_1_write_time_2f8771d6, RMask;
  wire [6:0] KDB_DATA_5ab16293, TTY_DATA_abb9d6ab;
  wire [15:0] Addr, LAddr, RAddr;
  wire [31:0] I0, I1, I2, I3, LData, ram_1_data_out_0_432456c9, ram_1_data_out_1_72dc7116,
       ram_1_data_out_2_130e6ee2, ram_1_data_out_3_bbf543c8, RI0, RI1, RI2, RI3;

  TTY #(.cols(80), .rows(25)) tty_1 (.data(TTY_DATA_abb9d6ab), .clk(CLK), .we(TTY_EN_70a2b517), .clr(RST));
  not not_1 (LoadRAMOn, ram_dispatcher_8f9b374a_1_finished);
  RAM_Dispatcher_8f9b374a ram_dispatcher_8f9b374a_1 (
    .Data(LData), .Address(LAddr), .Mask(LMask), .Finished(ram_dispatcher_8f9b374a_1_finished), .Write(LW),
    .Clock(CLK), .CLR(LCLR), .WriteTime(ram_1_write_time_2f8771d6));
  Keyboard #(.buflen(64)) keyboard_1 (.clk(CLK), .re(KDB[0]), .avail(KDB[2]), .data(KDB_DATA_5ab16293));  // open: clr
  RAM ram_1 (
    .Data_Out_0_432456c9(ram_1_data_out_0_432456c9), .Data_Out_1_72dc7116(ram_1_data_out_1_72dc7116),
    .Data_Out_2_130e6ee2(ram_1_data_out_2_130e6ee2), .Data_Out_3_bbf543c8(ram_1_data_out_3_bbf543c8),
    .Read_Time_acdb67b1(ram_1_read_time_acdb67b1), .Write_Time_2f8771d6(ram_1_write_time_2f8771d6),
    .Address(RAddr), .Data_In_0_579f9a88(RI0), .Data_In_1_bf2fe127(RI1), .Data_In_2_4041f204(RI2),
    .Data_In_3_88a85a1a(RI3), .Mask(RMask), .NOT_Read_Write_fb3b76d9(R_R_W_3abe9cfd),
    .Chip_Select_faaddd0a(RCS), .Reset(button_1_out));
  Button button_1 (.out(button_1_out));
  D_Flip_Flop d_ff_1 (.clk(CLK), .D(1'b1), .Q(d_ff_1_q), .reset(Reset_out));  // open: Qn, preset
  Button Reset (.out(Reset_out));
  S_MIPS_5880dd0a s_mips_5880dd0a_1 (
    .NOT_Read_Write_fb3b76d9(R_W_ea6840f6), .Chip_Select_faaddd0a(CS), .RAM_In_0_05162c2c(I0),
    .Address(Addr), .RAM_In_1_6afd0ef1(I1), .RAM_In_2_3f4e9933(I2), .RAM_In_3_c6f2f544(I2), .Mask(Mask),
    .TTY_Enable_58b476f8(TTY_EN_70a2b517), .TTY_ASCII_Data_10878087(TTY_DATA_abb9d6ab), .Stop(halt),
    .Kbd_Enable_158e6822(KDB[0]), .Kbd_Clear_7b2e70da(KDB[1]),
    .RAM_Out_0_374683a7(ram_1_data_out_0_432456c9), .RAM_Out_1_e9069e2f(ram_1_data_out_1_72dc7116),
    .RAM_Out_2_520e9480(ram_1_data_out_2_130e6ee2), .RAM_Out_3_f1b7199a(ram_1_data_out_3_bbf543c8),
    .Read_Time_acdb67b1(ram_1_read_time_acdb67b1), .Write_Time_2f8771d6(ram_1_write_time_2f8771d6),
    .Kbd_Available_8439e4a8(KDB[2]), .Kbd_ASCII_Data_efad2076(KDB_DATA_5ab16293), .Reset(RST), .Clock(CLK));
  D_Flip_Flop d_ff_2 (.preset(LCLR), .reset(LoadRAM));  // open: D, clk, Q, Qn
  or or_1 (RST, LCLR, LoadRAM);
  Clock clock_1 (.out(CLK));
  Multiplexer #(.enable("true"), .width(32)) multiplexer_1 (
    .in0(I0), .in1(LData), .out(RI0), .sel(LoadRAM));  // open: en
  Multiplexer #(.enable("true"), .width(32)) multiplexer_2 (
    .in0(I1), .in1(LData), .out(RI1), .sel(LoadRAM));  // open: en
  Multiplexer #(.enable("true"), .width(32)) multiplexer_3 (
    .in0(I2), .in1(LData), .out(RI2), .sel(LoadRAM));  // open: en
  Multiplexer #(.enable("true"), .width(32)) multiplexer_4 (
    .in0(I3), .in1(LData), .out(RI3), .sel(LoadRAM));  // open: en
  and and_1 (LoadRAM, ~DESHABILITAR_DISPATCHER_e4100c26, LoadRAMOn);  // AND_Gate
  Multiplexer #(.enable("true"), .width(16)) multiplexer_5 (
    .in0(Addr), .in1(LAddr), .out(RAddr), .sel(LoadRAM));  // open: en
  Multiplexer #(.enable("true"), .width(4)) multiplexer_6 (
    .in0(Mask), .in1(LMask), .out(RMask), .sel(LoadRAM));  // open: en
  Multiplexer #(.enable("true")) multiplexer_7 (.in0(CS), .in1(LW), .out(RCS), .sel(LoadRAM));  // open: en
  Multiplexer #(.enable("true")) multiplexer_8 (
    .in0(R_W_ea6840f6), .in1(LW), .out(R_R_W_3abe9cfd), .sel(LoadRAM));  // open: en

  // Notes on the sheet:
  //   NO MODIFICAR
  //   Keyboard
endmodule

module RAM (
  input  [15:0] Address,
  input  [31:0] Data_In_0_579f9a88,
  input  [31:0] Data_In_1_bf2fe127,
  input  [31:0] Data_In_2_4041f204,
  input  [31:0] Data_In_3_88a85a1a,
  input  [3:0] Mask,
  input  NOT_Read_Write_fb3b76d9,
  input  Chip_Select_faaddd0a,
  input  Reset,
  output [31:0] Data_Out_0_432456c9,
  output [31:0] Data_Out_1_72dc7116,
  output [31:0] Data_Out_2_130e6ee2,
  output [31:0] Data_Out_3_bbf543c8,
  output [3:0] Read_Time_acdb67b1,
  output [3:0] Write_Time_2f8771d6
);

  wire and_2_out, and_3_out, and_4_out, and_5_out, and_6_out, and_7_out, and_8_out, and_9_out, Changed, CLK,
       comparator_2_eq, comparator_3_eq, comparator_4_eq, comparator_5_eq, comparator_6_eq, Count,
       demultiplexer_3_out0, Idle, Idle_q, Load, Load0, Load1, nand_1_out, or_1_out, or_2_out, or_3_out,
       or_4_out, or_5_out, or_6_out, or_7_out, or_8_out, or_9_out, or_10_out, undriven, Update_Mem_91597652,
       Zero_Time_7f1a938a;
  wire [3:0] counter_1_q, multiplexer_1_out, subtractor_1_out;
  wire [31:0] register_1_q, register_2_q, register_3_q, register_4_q, register_5_q;

  // Probe on 4'b0011
  // Probe on 4'b0010
  Multiplexer #(.enable("true"), .width(4)) multiplexer_1 (
    .in0(4'b0011), .in1(4'b0010), .out(multiplexer_1_out), .sel(NOT_Read_Write_fb3b76d9));  // open: en
  or or_1 (or_1_out, Idle, Update_Mem_91597652);
  or or_2 (or_2_out, ~Chip_Select_faaddd0a, Reset);  // OR_Gate
  Subtractor #(.width(4)) subtractor_1 (.a(multiplexer_1_out), .b(4'b0010), .out(subtractor_1_out));  // open: bin, bout
  Demultiplexer #(.enable("true")) demultiplexer_1 (.out0(Idle), .out1(Load0), .in(Idle_q), .sel(Changed));  // open: en
  D_Flip_Flop u_Idle (.clk(CLK), .D(or_1_out), .Q(Idle_q), .preset(or_2_out));  // open: Qn, reset
  // Probe on counter_1_q
  Counter #(.max('hf), .width(4)) counter_1 (
    .load(Load), .D(subtractor_1_out), .count(Count), .Q(counter_1_q), .clk(CLK), .clr(or_3_out));  // open: carry, up
  or or_3 (or_3_out, ~Chip_Select_faaddd0a, Reset);  // OR_Gate
  Comparator #(.mode("unsigned"), .width(4)) comparator_1 (
    .a(4'b0000), .b(counter_1_q), .eq(Zero_Time_7f1a938a));  // open: gt, lt
  or or_4 (or_4_out, Count, Load0, Load1);
  Register #(.width(32)) register_1 (
    .D(Data_In_0_579f9a88), .en(Chip_Select_faaddd0a), .Q(register_1_q), .clk(CLK), .clr(or_5_out));
  or or_5 (or_5_out, ~Chip_Select_faaddd0a, Reset);  // OR_Gate
  Register #(.width(32)) register_2 (
    .D(Data_In_1_bf2fe127), .en(Chip_Select_faaddd0a), .Q(register_2_q), .clk(CLK), .clr(or_6_out));
  or or_6 (or_6_out, ~Chip_Select_faaddd0a, Reset);  // OR_Gate
  Register #(.width(32)) register_3 (
    .D(Data_In_2_4041f204), .en(Chip_Select_faaddd0a), .Q(register_3_q), .clk(CLK), .clr(or_7_out));
  or or_7 (or_7_out, ~Chip_Select_faaddd0a, Reset);  // OR_Gate
  Register #(.width(32)) register_4 (
    .D(Data_In_3_88a85a1a), .en(Chip_Select_faaddd0a), .Q(register_4_q), .clk(CLK), .clr(or_8_out));
  or or_8 (or_8_out, ~Chip_Select_faaddd0a, Reset);  // OR_Gate
  Register #(.width(32)) register_5 (
    .D({{11{1'b1}}, NOT_Read_Write_fb3b76d9, Mask, Address}), .en(Chip_Select_faaddd0a), .Q(register_5_q),
    .clk(CLK), .clr(or_9_out));
  or or_9 (or_9_out, ~Chip_Select_faaddd0a, Reset);  // OR_Gate
  D_Flip_Flop Proc (.clk(or_10_out), .Q(Load1), .preset(undriven));  // open: D, Qn, reset
  or or_10 (or_10_out, ~Chip_Select_faaddd0a, Reset);  // OR_Gate
  Demultiplexer #(.enable("true")) demultiplexer_2 (
    .out0(Count), .out1(Update_Mem_91597652), .in(demultiplexer_3_out0), .sel(Zero_Time_7f1a938a));  // open: en
  Demultiplexer #(.enable("true")) demultiplexer_3 (
    .out0(demultiplexer_3_out0), .out1(Load1), .in(undriven), .sel(Changed));  // open: en
  Clock clock_1 (.out(CLK));
  Comparator #(.width(32)) comparator_2 (
    .a(register_1_q), .b(Data_In_0_579f9a88), .eq(comparator_2_eq));  // open: gt, lt
  Comparator #(.width(32)) comparator_3 (
    .a(register_2_q), .b(Data_In_1_bf2fe127), .eq(comparator_3_eq));  // open: gt, lt
  Comparator #(.width(32)) comparator_4 (
    .a(register_3_q), .b(Data_In_2_4041f204), .eq(comparator_4_eq));  // open: gt, lt
  Comparator #(.width(32)) comparator_5 (
    .a(register_4_q), .b(Data_In_3_88a85a1a), .eq(comparator_5_eq));  // open: gt, lt
  Comparator #(.width(32)) comparator_6 (
    .a(register_5_q), .b({{11{1'b1}}, NOT_Read_Write_fb3b76d9, Mask, Address}), .eq(comparator_6_eq));  // open: gt, lt
  nand nand_1 (nand_1_out, comparator_2_eq, comparator_4_eq);
  and and_1 (Changed, nand_1_out, Chip_Select_faaddd0a);
  or or_11 (Load, Count, Load1, Load0);
  and and_2 (and_2_out, Mask[0], Update_Mem_91597652, NOT_Read_Write_fb3b76d9);
  and and_3 (and_3_out, Mask[1], Update_Mem_91597652, NOT_Read_Write_fb3b76d9);
  and and_4 (and_4_out, Mask[2], Update_Mem_91597652, NOT_Read_Write_fb3b76d9);
  and and_5 (and_5_out, Mask[3], Update_Mem_91597652, NOT_Read_Write_fb3b76d9);
  RAM_part #(.addrWidth(16), .dataWidth(32)) ram_1 (
    .addr(Address), .data(Data_Out_0_432456c9), .sel(Chip_Select_faaddd0a), .clk(CLK), .ld(and_6_out),
    .clr(Reset));
  and and_6 (and_6_out, ~NOT_Read_Write_fb3b76d9, Idle);  // AND_Gate
  RAM_part #(.addrWidth(16), .dataWidth(32)) ram_2 (
    .addr(Address), .data(Data_Out_1_72dc7116), .sel(Chip_Select_faaddd0a), .clk(CLK), .ld(and_7_out),
    .clr(Reset));
  and and_7 (and_7_out, ~NOT_Read_Write_fb3b76d9, Idle);  // AND_Gate
  RAM_part #(.addrWidth(16), .dataWidth(32)) ram_3 (
    .addr(Address), .data(Data_Out_2_130e6ee2), .sel(Chip_Select_faaddd0a), .clk(CLK), .ld(and_8_out),
    .clr(Reset));
  and and_8 (and_8_out, ~NOT_Read_Write_fb3b76d9, Idle);  // AND_Gate
  RAM_part #(.addrWidth(16), .dataWidth(32)) ram_4 (
    .addr(Address), .data(Data_Out_3_bbf543c8), .sel(Chip_Select_faaddd0a), .clk(CLK), .ld(and_9_out),
    .clr(Reset));
  and and_9 (and_9_out, ~NOT_Read_Write_fb3b76d9, Idle);  // AND_Gate

  assign Read_Time_acdb67b1 = 4'b0011;
  assign Write_Time_2f8771d6 = 4'b0010;

  // Other names for the same wires on the sheet: M0 = Mask[0]; M1 = Mask[1]; M2 = Mask[2]; M3 = Mask[3];
  //   RW = NOT_Read_Write_fb3b76d9; CLR = Reset; CS = Chip_Select_faaddd0a; Load2 = Count

  // Notes on the sheet:
  //   NO MODIFICAR
  //   excepto quizás los valores RT y WT
  //   BANK0
  //   BANK1
  //   BANK2
  //   BANK3
endmodule

module S_MIPS_5880dd0a (
  input  Kbd_Available_8439e4a8,
  input  [6:0] Kbd_ASCII_Data_efad2076,
  input  [31:0] RAM_Out_0_374683a7,
  input  [31:0] RAM_Out_1_e9069e2f,
  input  Reset,
  input  [31:0] RAM_Out_2_520e9480,
  input  Clock,
  input  [31:0] RAM_Out_3_f1b7199a,
  input  [3:0] Read_Time_acdb67b1,
  input  [3:0] Write_Time_2f8771d6,
  output Kbd_Enable_158e6822,
  output [15:0] Address,
  output Kbd_Clear_7b2e70da,
  output TTY_Enable_58b476f8,
  output [6:0] TTY_ASCII_Data_10878087,
  output Stop,
  output [31:0] RAM_In_0_05162c2c,
  output [31:0] RAM_In_1_6afd0ef1,
  output [31:0] RAM_In_2_3f4e9933,
  output [31:0] RAM_In_3_c6f2f544,
  output [3:0] Mask,
  output NOT_Read_Write_fb3b76d9,
  output Chip_Select_faaddd0a
);


  // Other names for the same wires on the sheet: CLK = Clock; CLR = Reset; CS = Chip_Select_faaddd0a;
  //   KBD_AVAIL_2266db55 = Kbd_Available_8439e4a8; KBD_CLR_4def20a2 = Kbd_Clear_7b2e70da;
  //   KBD_DATA_e6f6b814[6:0] = Kbd_ASCII_Data_efad2076; KBD_ENABLE_efa12e9d = Kbd_Enable_158e6822;
  //   RAM_A_44a06955[15:0] = Address; RAM_INPUT_0_a7bed6e4[31:0] = RAM_In_0_05162c2c;
  //   RAM_INPUT_1_4af4ef62[31:0] = RAM_In_1_6afd0ef1; RAM_INPUT_2_41b4053a[31:0] = RAM_In_2_3f4e9933;
  //   RAM_INPUT_3_2eafb6f8[31:0] = RAM_In_3_c6f2f544; RAM_MASK_8a291bcb[3:0] = Mask;
  //   RAM_OUTPUT_0_2c37567b[31:0] = RAM_Out_0_374683a7; RAM_OUTPUT_1_0510ba8b[31:0] = RAM_Out_1_e9069e2f;
  //   RAM_OUTPUT_2_26a6014a[31:0] = RAM_Out_2_520e9480; RAM_OUTPUT_3_c4c4e2d8[31:0] = RAM_Out_3_f1b7199a;
  //   RW = NOT_Read_Write_fb3b76d9; TTY_DATA_abb9d6ab[6:0] = TTY_ASCII_Data_10878087;
  //   TTY_ENABLE_8d58bebb = TTY_Enable_58b476f8

  // Notes on the sheet:
  //   RAM ADDRESS
  //   DATA FROM RAM
  //   DATA TO RAM
  //   DATA WRITE MASK
  //   RAM TIMING
  //   RAM CONTROL
  //   KEYBOARD
  //   TTY
  //   SEQUENCING
endmodule

module RAM_Dispatcher_8f9b374a (
  input  [3:0] WriteTime,
  input  Clock,
  input  CLR,
  output [31:0] Data,
  output [15:0] Address,
  output [3:0] Mask,
  output Finished,
  output Write
);

  wire demultiplexer_2_out1, demultiplexer_3_out1, End, IDLE_q, IncAddr, Load, or_1_out, or_2_out, undriven,
       WriteEnd;
  wire [3:0] counter_1_q;
  wire [31:0] CurrentAddress_q;

  Counter #(.max('hffffffff), .width(32)) CurrentAddress (
    .count(IncAddr), .Q({CurrentAddress_q[31:18], Address, CurrentAddress_q[1:0]}), .clk(Clock), .clr(CLR));  // open: load, D, carry, up
  or or_1 (or_1_out, IncAddr, demultiplexer_3_out1, Finished);
  D_Flip_Flop IDLE (.clk(Clock), .D(or_1_out), .Q(IDLE_q), .preset(CLR));  // open: Qn, reset
  Demultiplexer #(.enable("true")) demultiplexer_1 (.out0(Load), .out1(Finished), .in(IDLE_q), .sel(End));  // open: en
  D_Flip_Flop While (.clk(CLR), .preset(undriven));  // open: D, Q, Qn, reset
  or or_2 (or_2_out, Write, Load);
  RAM_part #(.addrWidth(18), .dataWidth(32)) ram_1 (
    .addr({Address, CurrentAddress_q[1:0]}), .data(Data), .clk(Clock));  // open: sel, ld, clr
  Demultiplexer #(.enable("true")) demultiplexer_2 (
    .out0(Write), .out1(demultiplexer_2_out1), .in(undriven), .sel(WriteEnd));  // open: en
  Decoder #(.select(2)) decoder_1 (
    .out0(Mask[0]), .out1(Mask[1]), .out2(Mask[2]), .out3(Mask[3]), .sel(CurrentAddress_q[1:0]));  // open: en
  Demultiplexer #(.enable("true")) demultiplexer_3 (
    .out0(IncAddr), .out1(demultiplexer_3_out1), .in(demultiplexer_2_out1), .sel(End));  // open: en
  Counter #(.max('hf), .width(4)) counter_1 (
    .load(Load), .D(WriteTime), .count(Write), .Q(counter_1_q), .clk(Clock));  // open: carry, up, clr
  Comparator #(.width(32)) comparator_1 (.a(Data), .b({32{1'b1}}), .eq(End));  // open: gt, lt
  Comparator #(.width(4)) comparator_2 (.a(4'b0000), .b(counter_1_q), .eq(WriteEnd));  // open: gt, lt

  // Other names for the same wires on the sheet: CLK = Clock; Count = Write; WT[3:0] = WriteTime
endmodule

module ALU (
  input  [3:0] in_1,
  input  [31:0] in_2,
  input  [31:0] in_3,
  output [31:0] out_4,
  output [31:0] out_5,
  output out_6,
  output out_7
);

  wire adder_1_cout, comparator_1_lt, comparator_2_lt, subtractor_1_bout, undriven;
  wire [31:0] op_and, op_div, op_div_rm, op_mul, op_mul_s, op_nor, op_or, op_shift, op_sub, op_sub_rm,
       op_sum, op_sum_rm, op_udiv, op_udiv_r, op_umul_hi, op_umul_lo, op_ushift, op_xor;

  assign op_and = in_2 & in_3;  // AND_Gate and_1, 32 bits wide
  assign op_or = in_2 | in_3;  // OR_Gate or_1, 32 bits wide
  assign op_nor = ~(in_2 | in_3);  // NOR_Gate nor_1, 32 bits wide
  assign op_xor = in_2 ^ in_3;  // XOR_Gate xor_1, 32 bits wide
  Comparator #(.width(32)) comparator_1 (.a(in_2), .b(in_3), .lt(comparator_1_lt));  // open: gt, eq
  assign op_shift = {{31{comparator_1_lt}}, comparator_1_lt};  // Bit_Extender bit_extender_1
  Comparator #(.mode("unsigned"), .width(32)) comparator_2 (.a(in_2), .b(in_3), .lt(comparator_2_lt));  // open: gt, eq
  assign op_ushift = {{31{comparator_2_lt}}, comparator_2_lt};  // Bit_Extender bit_extender_2
  Adder #(.width(32)) adder_1 (.a(in_2), .b(in_3), .out(op_sum), .cout(adder_1_cout));  // open: cin
  assign op_sum_rm = {{31{adder_1_cout}}, adder_1_cout};  // Bit_Extender bit_extender_3
  Subtractor #(.width(32)) subtractor_1 (.a(in_2), .b(in_3), .out(op_sub), .bin(undriven), .bout(subtractor_1_bout));
  assign op_sub_rm = {{31{subtractor_1_bout}}, subtractor_1_bout};  // Bit_Extender bit_extender_4
  Multiplier #(.width(32)) multiplier_1 (.a(in_2), .b(in_3), .out(op_mul), .cout(op_mul_s));  // open: cin
  Divider #(.width(32)) divider_1 (.a(in_2), .b(in_3), .out(op_udiv), .rem(op_udiv_r));  // open: upper
  umul umul_1 (.Hi(op_umul_hi), .Lo(op_umul_lo), .B(in_3), .A(in_2));
  div div_1 (.RESTO(op_div_rm), .COCIENTE(op_div), .DIVIDENDO(in_2), .DIVISOR(in_3));
  Multiplexer #(.enable("true"), .select(4), .width(32)) multiplexer_1 (
    .in0(op_sum), .in1(op_sub), .in2(op_mul), .in3(op_umul_lo), .in4(op_div), .in5(op_udiv), .in6(op_and),
    .in7(op_or), .in8(op_xor), .in9(op_nor), .in10(op_shift), .in11(op_ushift), .out(out_5), .sel(in_1));  // open: in12, in13, in14, in15, en
  Multiplexer #(.enable("true"), .select(4), .width(32)) multiplexer_2 (
    .in0(op_sum_rm), .in1(op_sub_rm), .in2(op_mul_s), .in3(op_umul_hi), .in4(op_div_rm), .in5(op_udiv_r),
    .in6({32{1'b0}}), .in7({32{1'b0}}), .in8({32{1'b0}}), .in9({32{1'b0}}), .in10({32{1'b0}}),
    .in11({32{1'b0}}), .out(out_4), .sel(in_1));  // open: in12, in13, in14, in15, en
  Comparator #(.width(32)) comparator_3 (.a(out_5), .b({32{1'b0}}), .eq(out_6), .lt(out_7));  // open: gt

  // Other names for the same wires on the sheet: in_1_t[31:0] = in_2; in_2_t[31:0] = in_3; op_code[3:0] = in_1;
  //   out_rm[31:0] = out_4; out_rs[31:0] = out_5
endmodule

module umul (
  input  [31:0] A,
  input  [31:0] B,
  output [31:0] Hi,
  output [31:0] Lo
);

  wire adder_1_cout, adder_3_cout, adder_5_cout, adder_8_cout, ps;
  wire [0:0] multiplexer_1_out, multiplexer_2_out;
  wire [1:0] Hi1;
  wire [29:0] Lo0;
  wire [30:0] A1, B1;
  wire [31:0] adder_2_out, adder_3_out, adder_6_out, adder_9_out, Hi0, HiImp, HiParA, HiParB, LoImp, LoParA,
       LoParB, multiplexer_3_out, multiplexer_4_out, remp, resp, subtractor_1_out, subtractor_2_out;

  Multiplier #(.width(32)) multiplier_1 (.a(A), .b(B), .out(resp), .cout(remp));  // open: cin
  Multiplier #(.width(32)) multiplier_2 (.a({1'b0, A1}), .b({1'b0, B1}), .out({Hi1, Lo0}), .cout(Hi0));  // open: cin
  Adder #(.width(32)) adder_1 (.a({Lo0, 2'b00}), .b({A1, 1'b0}), .out(LoParB), .cout(adder_1_cout));  // open: cin
  Adder #(.width(32)) adder_2 (.a({Hi0[29:0], Hi1}), .b({32{1'b0}}), .out(adder_2_out));  // open: cin, cout
  Adder #(.width(32)) adder_3 (.a({B1, 1'b0}), .b(LoParB), .out(adder_3_out), .cout(adder_3_cout));  // open: cin
  Adder #(.width(32)) adder_4 (.a({32{1'b0}}), .b(adder_2_out), .out(HiParB), .cin(adder_1_cout));  // open: cout
  nor nor_1 (ps, A[31], B[31]);
  Adder #(.width(32)) adder_5 (.a(adder_3_out), .b(32'h1), .out(LoImp), .cout(adder_5_cout));  // open: cin
  Adder #(.width(32)) adder_6 (.a(HiParB), .b({32{1'b0}}), .out(adder_6_out), .cin(adder_3_cout));  // open: cout
  Subtractor #(.width(32)) subtractor_1 (.a(32'h1), .b(B), .out(subtractor_1_out));  // open: bin, bout
  Adder #(.width(32)) adder_7 (.a({32{1'b0}}), .b(adder_6_out), .out(HiImp), .cin(adder_5_cout));  // open: cout
  Multiplexer #(.enable("true"), .width(32)) multiplexer_1 (
    .in0(A), .in1(subtractor_2_out), .out({A1, multiplexer_1_out[0]}), .sel(A[0]));  // open: en
  Subtractor #(.width(32)) subtractor_2 (.a(32'h1), .b(A), .out(subtractor_2_out));  // open: bin, bout
  Multiplexer #(.enable("true"), .width(32)) multiplexer_2 (
    .in0(B), .in1(subtractor_1_out), .out({B1, multiplexer_2_out[0]}), .sel(B[0]));  // open: en
  Adder #(.width(32)) adder_8 (.a({Lo0, 2'b00}), .b({B1, 1'b0}), .out(LoParA), .cout(adder_8_cout));  // open: cin
  Adder #(.width(32)) adder_9 (.a({Hi0[29:0], Hi1}), .b({32{1'b0}}), .out(adder_9_out));  // open: cin, cout
  Adder #(.width(32)) adder_10 (.a({32{1'b0}}), .b(adder_9_out), .out(HiParA), .cin(adder_8_cout));  // open: cout
  Multiplexer #(.enable("true"), .select(2), .width(32)) multiplexer_3 (
    .in0({Hi0[29:0], Hi1}), .in1(HiParA), .in2(HiParB), .in3(HiImp), .out(multiplexer_3_out),
    .sel({B[0], A[0]}));  // open: en
  Multiplexer #(.enable("true"), .select(2), .width(32)) multiplexer_4 (
    .in0({Lo0, 2'b00}), .in1(LoParA), .in2(LoParB), .in3(LoImp), .out(multiplexer_4_out), .sel({B[0], A[0]}));  // open: en
  Multiplexer #(.enable("true"), .width(32)) multiplexer_5 (
    .in0(multiplexer_3_out), .in1(remp), .out(Hi), .sel(ps));  // open: en
  Multiplexer #(.enable("true"), .width(32)) multiplexer_6 (
    .in0(multiplexer_4_out), .in1(resp), .out(Lo), .sel(ps));  // open: en

  // Other names for the same wires on the sheet: AP = A[0]; BP = B[0]; nega = A[31]; A2Lo[31:1] = A1; negb = B[31];
  //   B2Lo[31:1] = B1; Hi1[31:2] = Hi0[29:0]; Lo0[31:30] = Hi1; Lo1[31:2] = Lo0
endmodule

module div (
  input  [31:0] DIVIDENDO,
  input  [31:0] DIVISOR,
  output [31:0] COCIENTE,
  output [31:0] RESTO
);

  wire xor_1_out;
  wire [31:0] adder_1_out, C, not_44_out, not_64_out, RESTO_t;

  not not_1 (not_44_out[31], RESTO_t[31]);
  not not_2 (not_44_out[30], RESTO_t[30]);
  not not_3 (not_44_out[29], RESTO_t[29]);
  not not_4 (not_44_out[28], RESTO_t[28]);
  not not_5 (not_44_out[27], RESTO_t[27]);
  Divider #(.width(32)) divider_1 (.a(DIVIDENDO), .b(DIVISOR), .out(C), .rem(RESTO_t));  // open: upper
  not not_6 (not_44_out[26], RESTO_t[26]);
  not not_7 (not_44_out[25], RESTO_t[25]);
  not not_8 (not_44_out[24], RESTO_t[24]);
  not not_9 (not_44_out[23], RESTO_t[23]);
  not not_10 (not_44_out[22], RESTO_t[22]);
  not not_11 (not_44_out[21], RESTO_t[21]);
  not not_12 (not_44_out[20], RESTO_t[20]);
  not not_13 (not_44_out[19], RESTO_t[19]);
  not not_14 (not_44_out[18], RESTO_t[18]);
  not not_15 (not_44_out[17], RESTO_t[17]);
  not not_16 (not_44_out[16], RESTO_t[16]);
  not not_17 (not_44_out[15], RESTO_t[15]);
  not not_18 (not_44_out[14], RESTO_t[14]);
  not not_19 (not_44_out[13], RESTO_t[13]);
  not not_20 (not_44_out[12], RESTO_t[12]);
  not not_21 (not_44_out[11], RESTO_t[11]);
  not not_22 (not_64_out[31], C[31]);
  not not_23 (not_64_out[30], C[30]);
  not not_24 (not_64_out[29], C[29]);
  not not_25 (not_64_out[28], C[28]);
  not not_26 (not_44_out[10], RESTO_t[10]);
  not not_27 (not_44_out[9], RESTO_t[9]);
  not not_28 (not_44_out[8], RESTO_t[8]);
  not not_29 (not_44_out[7], RESTO_t[7]);
  not not_30 (not_44_out[6], RESTO_t[6]);
  not not_31 (not_44_out[5], RESTO_t[5]);
  not not_32 (not_44_out[4], RESTO_t[4]);
  not not_33 (not_44_out[3], RESTO_t[3]);
  not not_34 (not_64_out[27], C[27]);
  not not_35 (not_64_out[26], C[26]);
  not not_36 (not_64_out[25], C[25]);
  not not_37 (not_64_out[24], C[24]);
  not not_38 (not_64_out[23], C[23]);
  not not_39 (not_64_out[22], C[22]);
  not not_40 (not_64_out[21], C[21]);
  not not_41 (not_64_out[20], C[20]);
  not not_42 (not_44_out[2], RESTO_t[2]);
  not not_43 (not_44_out[1], RESTO_t[1]);
  not not_44 (not_44_out[0], RESTO_t[0]);
  not not_45 (not_64_out[19], C[19]);
  not not_46 (not_64_out[18], C[18]);
  not not_47 (not_64_out[17], C[17]);
  not not_48 (not_64_out[16], C[16]);
  not not_49 (not_64_out[15], C[15]);
  not not_50 (not_64_out[14], C[14]);
  not not_51 (not_64_out[13], C[13]);
  not not_52 (not_64_out[12], C[12]);
  Multiplexer #(.enable("true"), .width(32)) multiplexer_1 (
    .in0(RESTO_t), .in1(not_44_out), .out(RESTO), .sel(DIVIDENDO[31]));  // open: en
  not not_53 (not_64_out[11], C[11]);
  not not_54 (not_64_out[10], C[10]);
  not not_55 (not_64_out[9], C[9]);
  not not_56 (not_64_out[8], C[8]);
  not not_57 (not_64_out[7], C[7]);
  not not_58 (not_64_out[6], C[6]);
  not not_59 (not_64_out[5], C[5]);
  not not_60 (not_64_out[4], C[4]);
  not not_61 (not_64_out[3], C[3]);
  not not_62 (not_64_out[2], C[2]);
  not not_63 (not_64_out[1], C[1]);
  not not_64 (not_64_out[0], C[0]);
  Adder #(.width(32)) adder_1 (.a(not_64_out), .b(32'h1), .out(adder_1_out));  // open: cin, cout
  xor xor_1 (xor_1_out, DIVIDENDO[31], DIVISOR[31]);
  Multiplexer #(.enable("true"), .width(32)) multiplexer_2 (
    .in0(C), .in1(adder_1_out), .out(COCIENTE), .sel(xor_1_out));  // open: en

  // Other names for the same wires on the sheet: A[31:0] = DIVIDENDO; SA = DIVIDENDO[31]; B[31:0] = DIVISOR;
  //   SB = DIVISOR[31]
endmodule

module RF (
  input  in_1,
  input  in_2,
  input  in_3,
  input  in_4,
  input  [31:0] in_5,
  input  in_6,
  input  in_7,
  input  [31:0] in_8,
  input  [31:0] in_9,
  input  [31:0] in_10,
  input  [31:0] in_11,
  input  [31:0] in_12,
  input  [4:0] in_13,
  input  [4:0] in_14,
  input  [4:0] in_15,
  input  [2:0] in_16,
  output [31:0] out_17,
  output [31:0] out_18,
  output [31:0] out_19
);

  wire and_1_out, and_2_out, and_3_out, and_4_out, and_5_out, and_6_out, and_7_out, and_8_out, and_9_out,
       and_10_out, and_11_out, and_12_out, and_13_out, and_14_out, and_15_out, and_16_out, and_17_out,
       and_18_out, and_19_out, and_20_out, and_21_out, and_22_out, and_23_out, and_24_out, and_25_out,
       and_26_out, and_27_out, and_28_out, and_29_out, and_30_out, and_31_out, and_32_out, fstack, h0, h1,
       h2, h3, h4, h5, h6, h7, h8, h9, h10, h11, h12, h13, h14, h15, h16, h17, h18, h19, h20, h21, h22, h23,
       h24, h25, h26, h27, h28, h29, h30, h31, or_1_out;
  wire [31:0] adder_1_out, inp, r0, r1, r2, r3, r4, r5, r6, r7, r8, r9, r10, r11, r12, r13, r14, r15, r16,
       r17, r18, r19, r20, r21, r22, r23, r24, r25, r26, r27, r28, r29, r30, sp, stack, subtractor_1_out;

  Decoder #(.enable("false"), .select(5)) decoder_1 (
    .out0(h0), .out1(h1), .out2(h2), .out3(h3), .out4(h4), .out5(h5), .out6(h6), .out7(h7), .out8(h8),
    .out9(h9), .out10(h10), .out11(h11), .out12(h12), .out13(h13), .out14(h14), .out15(h15), .out16(h16),
    .out17(h17), .out18(h18), .out19(h19), .out20(h20), .out21(h21), .out22(h22), .out23(h23), .out24(h24),
    .out25(h25), .out26(h26), .out27(h27), .out28(h28), .out29(h29), .out30(h30), .out31(h31), .sel(in_13));
  Multiplexer #(.enable("true"), .select(3), .width(32)) multiplexer_1 (
    .in0(in_9), .in1(in_10), .in2(in_11), .in3(in_12), .in4(in_8), .in5(in_5), .out(inp), .sel(in_16));  // open: in6, in7, en
  and and_1 (and_1_out, h0, in_3);
  and and_2 (and_2_out, h1, in_3);
  and and_3 (and_3_out, h2, in_3);
  and and_4 (and_4_out, h3, in_3);
  and and_5 (and_5_out, h4, in_3);
  and and_6 (and_6_out, h5, in_3);
  and and_7 (and_7_out, h6, in_3);
  and and_8 (and_8_out, h7, in_3);
  and and_9 (and_9_out, h8, in_3);
  and and_10 (and_10_out, h9, in_3);
  Register #(.width(32)) register_1 (.D(inp), .en(and_1_out), .Q(r0), .clk(in_1), .clr(in_2));
  Register #(.width(32)) register_2 (.D(inp), .en(and_2_out), .Q(r1), .clk(in_1), .clr(in_2));
  Register #(.width(32)) register_3 (.D(inp), .en(and_3_out), .Q(r2), .clk(in_1), .clr(in_2));
  Register #(.width(32)) register_4 (.D(inp), .en(and_4_out), .Q(r3), .clk(in_1), .clr(in_2));
  Register #(.width(32)) register_5 (.D(inp), .en(and_5_out), .Q(r4), .clk(in_1), .clr(in_2));
  Register #(.width(32)) register_6 (.D(inp), .en(and_6_out), .Q(r5), .clk(in_1), .clr(in_2));
  Register #(.width(32)) register_7 (.D(inp), .en(and_7_out), .Q(r6), .clk(in_1), .clr(in_2));
  Register #(.width(32)) register_8 (.D(inp), .en(and_8_out), .Q(r7), .clk(in_1), .clr(in_2));
  Register #(.width(32)) register_9 (.D(inp), .en(and_9_out), .Q(r8), .clk(in_1), .clr(in_2));
  Register #(.width(32)) register_10 (.D(inp), .en(and_10_out), .Q(r9), .clk(in_1), .clr(in_2));
  and and_11 (and_11_out, h10, in_3);
  and and_12 (and_12_out, h11, in_3);
  and and_13 (and_13_out, h12, in_3);
  and and_14 (and_14_out, h13, in_3);
  and and_15 (and_15_out, h14, in_3);
  and and_16 (and_16_out, h15, in_3);
  and and_17 (and_17_out, h16, in_3);
  and and_18 (and_18_out, h17, in_3);
  and and_19 (and_19_out, h18, in_3);
  and and_20 (and_20_out, h19, in_3);
  Register #(.width(32)) register_11 (.D(inp), .en(and_11_out), .Q(r10), .clk(in_1), .clr(in_2));
  Register #(.width(32)) register_12 (.D(inp), .en(and_12_out), .Q(r11), .clk(in_1), .clr(in_2));
  Register #(.width(32)) register_13 (.D(inp), .en(and_13_out), .Q(r12), .clk(in_1), .clr(in_2));
  Register #(.width(32)) register_14 (.D(inp), .en(and_14_out), .Q(r13), .clk(in_1), .clr(in_2));
  Register #(.width(32)) register_15 (.D(inp), .en(and_15_out), .Q(r14), .clk(in_1), .clr(in_2));
  Register #(.width(32)) register_16 (.D(inp), .en(and_16_out), .Q(r15), .clk(in_1), .clr(in_2));
  Register #(.width(32)) register_17 (.D(inp), .en(and_17_out), .Q(r16), .clk(in_1), .clr(in_2));
  Register #(.width(32)) register_18 (.D(inp), .en(and_18_out), .Q(r17), .clk(in_1), .clr(in_2));
  Register #(.width(32)) register_19 (.D(inp), .en(and_19_out), .Q(r18), .clk(in_1), .clr(in_2));
  Register #(.width(32)) register_20 (.D(inp), .en(and_20_out), .Q(r19), .clk(in_1), .clr(in_2));
  and and_21 (and_21_out, h20, in_3);
  and and_22 (and_22_out, h21, in_3);
  and and_23 (and_23_out, h22, in_3);
  and and_24 (and_24_out, h23, in_3);
  and and_25 (and_25_out, h24, in_3);
  and and_26 (and_26_out, h25, in_3);
  and and_27 (and_27_out, h26, in_3);
  and and_28 (and_28_out, h27, in_3);
  and and_29 (and_29_out, h28, in_3);
  and and_30 (and_30_out, h29, in_3);
  Register #(.width(32)) register_21 (.D(inp), .en(and_21_out), .Q(r20), .clk(in_1), .clr(in_2));
  Register #(.width(32)) register_22 (.D(inp), .en(and_22_out), .Q(r21), .clk(in_1), .clr(in_2));
  Register #(.width(32)) register_23 (.D(inp), .en(and_23_out), .Q(r22), .clk(in_1), .clr(in_2));
  Register #(.width(32)) register_24 (.D(inp), .en(and_24_out), .Q(r23), .clk(in_1), .clr(in_2));
  Register #(.width(32)) register_25 (.D(inp), .en(and_25_out), .Q(r24), .clk(in_1), .clr(in_2));
  Register #(.width(32)) register_26 (.D(inp), .en(and_26_out), .Q(r25), .clk(in_1), .clr(in_2));
  Register #(.width(32)) register_27 (.D(inp), .en(and_27_out), .Q(r26), .clk(in_1), .clr(in_2));
  Register #(.width(32)) register_28 (.D(inp), .en(and_28_out), .Q(r27), .clk(in_1), .clr(in_2));
  Register #(.width(32)) register_29 (.D(inp), .en(and_29_out), .Q(r28), .clk(in_1), .clr(in_2));
  Register #(.width(32)) register_30 (.D(inp), .en(and_30_out), .Q(r29), .clk(in_1), .clr(in_2));
  and and_31 (and_31_out, h20, in_3);
  and and_32 (and_32_out, h20, in_3);
  Adder #(.width(32)) adder_1 (.a(out_17), .b(32'h4), .out(adder_1_out));  // open: cin, cout
  Subtractor #(.width(32)) subtractor_1 (.a(out_17), .b(32'h4), .out(subtractor_1_out));  // open: bin, bout
  Multiplexer #(.enable("true"), .width(32)) multiplexer_2 (
    .in0(inp), .in1(stack), .out(sp), .sel(fstack));  // open: en
  Register #(.width(32)) register_31 (.D(inp), .en(and_31_out), .Q(r30), .clk(in_1), .clr(in_2));
  or or_1 (or_1_out, in_7, and_32_out);
  or or_2 (fstack, in_6, in_4);
  Multiplexer #(.enable("true"), .width(32)) multiplexer_3 (
    .in0(adder_1_out), .in1(subtractor_1_out), .out(stack), .sel(in_4));  // open: en
  Register #(.width(32)) register_32 (.D(inp), .en(or_1_out), .Q(out_17), .clk(in_1), .clr(in_2));
  Multiplexer #(.enable("true"), .select(5), .width(32)) multiplexer_4 (
    .in0(r0), .in1(r1), .in2(r2), .in3(r3), .in4(r4), .in5(r5), .in6(r6), .in7(r7), .in8(r8), .in9(r9),
    .in10(r10), .in11(r11), .in12(r12), .in13(r13), .in14(r14), .in15(r15), .in16(r16), .in17(r17),
    .in18(r18), .in19(r19), .in20(r20), .in21(r21), .in22(r22), .in23(r23), .in24(r24), .in25(r25),
    .in26(r26), .in27(r27), .in28(r28), .in29(r29), .in30(r30), .in31(out_17), .out(out_18), .sel(in_14));  // open: en
  Multiplexer #(.enable("true"), .select(5), .width(32)) multiplexer_5 (
    .in0(r0), .in1(r1), .in2(r2), .in3(r3), .in4(r4), .in5(r5), .in6(r6), .in7(r7), .in8(r8), .in9(r9),
    .in10(r10), .in11(r11), .in12(r12), .in13(r13), .in14(r14), .in15(r15), .in16(r16), .in17(r17),
    .in18(r18), .in19(r19), .in20(r20), .in21(r21), .in22(r22), .in23(r23), .in24(r24), .in25(r25),
    .in26(r26), .in27(r27), .in28(r28), .in29(r29), .in30(r30), .in31(out_17), .out(out_19), .sel(in_15));  // open: en

  // Other names for the same wires on the sheet: chgsp = in_7; clear = in_1; enabled = in_3; hi[31:0] = in_8;
  //   kb_data[31:0] = in_12; lo[31:0] = in_5; o1[31:0] = out_18; o2[31:0] = out_19; pop = in_6; push = in_4;
  //   r31[31:0] = out_17; ram_out[31:0] = in_11; res[31:0] = in_9; reset = in_2; rnd[31:0] = in_10
endmodule

module ID (
  input  [31:0] in_1,
  output [31:0] K,
  output [4:0] Sa,
  output [4:0] Sb,
  output [4:0] DA,
  output [2:0] DS,
  output [2:0] Jump,
  output [1:0] FC,
  output OS,
  output Mul_Div_1f10744c,
  output Op_const,
  output pop,
  output push,
  output nop,
  output halt,
  output tty,
  output rnd,
  output kbd,
  output [3:0] Op,
  output alu,
  output wrf,
  output lw,
  output sw
);

  wire add, addi, \and , and_30_out, and_41_out, and_42_out, andi, beq, bgtz, blez, bltz, bnq, div, divu,
       ins_i_dff40eef, ins_j_94783cf3, ins_r_fbe5be26, k1, k2, mfhi, mflo, mult, mulu, \nor , opand, opor,
       opslt, opsltu, opsub, opxor, \or , ori, R_espec, R_pila, R_simple, Rout, Rrs, slt, slti, sltiu, sltu,
       sub, \xor , xori;
  wire [1:0] selk;

  or or_1 (ins_r_fbe5be26, R_espec, R_simple, R_pila);
  and and_1 (R_espec, in_1[26], in_1[27], in_1[28], in_1[29], in_1[30], in_1[31]);
  and and_2 (R_simple, ~in_1[26], ~in_1[27], ~in_1[28], ~in_1[29], ~in_1[30], ~in_1[31]);  // AND_Gate
  and and_3 (R_pila, ~in_1[26], ~in_1[27], ~in_1[28], in_1[29], in_1[30], in_1[31]);  // AND_Gate
  and and_4 (nop, ~in_1[0], ~in_1[1], ~in_1[2], ~in_1[3], ~in_1[4], ~in_1[5], R_simple);  // AND_Gate
  and and_5 (add, ~in_1[0], ~in_1[1], ~in_1[2], ~in_1[3], ~in_1[4], in_1[5], R_simple);  // AND_Gate
  nor nor_1 (ins_i_dff40eef, ins_j_94783cf3, ins_r_fbe5be26);
  and and_6 (ins_j_94783cf3, ~in_1[26], in_1[27], ~in_1[28], ~in_1[29], ~in_1[30], ~in_1[31]);  // AND_Gate
  and and_7 (sub, ~in_1[0], in_1[1], ~in_1[2], ~in_1[3], ~in_1[4], in_1[5], R_simple);  // AND_Gate
  and and_8 (mult, ~in_1[0], ~in_1[1], ~in_1[2], in_1[3], in_1[4], ~in_1[5], R_simple);  // AND_Gate
  and and_9 (addi, ~in_1[26], ~in_1[27], ~in_1[28], in_1[29], ~in_1[30], ~in_1[31], ins_i_dff40eef);  // AND_Gate
  and and_10 (slti, ~in_1[26], in_1[27], ~in_1[28], in_1[29], ~in_1[30], ~in_1[31], ins_i_dff40eef);  // AND_Gate
  and and_11 (push, R_pila, in_1[0]);
  const_sel const_sel_1 (.in_1(k1), .in_2(k2), .in_3(ins_j_94783cf3), .out_4(selk[0]), .out_5(selk[1]));
  and and_12 (mulu, in_1[0], ~in_1[1], ~in_1[2], in_1[3], in_1[4], ~in_1[5], R_simple);  // AND_Gate
  and and_13 (div, ~in_1[0], in_1[1], ~in_1[2], in_1[3], in_1[4], ~in_1[5], R_simple);  // AND_Gate
  and and_14 (sltiu, in_1[26], in_1[27], ~in_1[28], in_1[29], ~in_1[30], ~in_1[31], ins_i_dff40eef);  // AND_Gate
  and and_15 (andi, ~in_1[26], ~in_1[27], in_1[28], in_1[29], ~in_1[30], ~in_1[31], ins_i_dff40eef);  // AND_Gate
  and and_16 (pop, ~in_1[0], R_pila);  // AND_Gate
  and and_17 (divu, in_1[0], in_1[1], ~in_1[2], in_1[3], in_1[4], ~in_1[5], R_simple);  // AND_Gate
  and and_18 (slt, ~in_1[0], in_1[1], ~in_1[2], in_1[3], ~in_1[4], in_1[5], R_simple);  // AND_Gate
  or or_2 (k1, sw, bnq, beq, bltz, lw, blez, bgtz, slti, sltiu, addi);
  or or_3 (opsub, sub, beq, bnq);
  or or_4 (opand, \and , andi);
  or or_5 (opsltu, sltiu, sltu);
  and and_19 (ori, in_1[26], ~in_1[27], in_1[28], in_1[29], ~in_1[30], ~in_1[31], ins_i_dff40eef);  // AND_Gate
  and and_20 (xori, ~in_1[26], in_1[27], in_1[28], in_1[29], ~in_1[30], ~in_1[31], ins_i_dff40eef);  // AND_Gate
  and and_21 (bltz, in_1[26], ~in_1[27], ~in_1[28], ~in_1[29], ~in_1[30], ~in_1[31], ins_i_dff40eef);  // AND_Gate
  and and_22 (sltu, in_1[0], in_1[1], ~in_1[2], in_1[3], ~in_1[4], in_1[5], R_simple);  // AND_Gate
  and and_23 (\and , ~in_1[0], ~in_1[1], in_1[2], ~in_1[3], ~in_1[4], in_1[5], R_simple);  // AND_Gate
  and and_24 (kbd, ~in_1[0], ~in_1[1], in_1[2], R_espec);  // AND_Gate
  and and_25 (lw, in_1[26], in_1[27], ~in_1[28], ~in_1[29], ~in_1[30], in_1[31], ins_i_dff40eef);  // AND_Gate
  and and_26 (sw, in_1[26], in_1[27], ~in_1[28], in_1[29], ~in_1[30], in_1[31], ins_i_dff40eef);  // AND_Gate
  or or_6 (k2, andi, xori, ori);
  or or_7 (opor, \or , bltz);
  or or_8 (opxor, \xor , xori);
  or or_9 (opslt, slt, slti);
  and and_27 (\or , in_1[0], ~in_1[1], in_1[2], ~in_1[3], ~in_1[4], in_1[5], R_simple);  // AND_Gate
  and and_28 (\nor , in_1[0], in_1[1], in_1[2], ~in_1[3], ~in_1[4], in_1[5], R_simple);  // AND_Gate
  and and_29 (halt, in_1[0], in_1[1], in_1[2], R_espec);
  and and_30 (and_30_out, R_simple, ~Mul_Div_1f10744c, ~nop, ~OS);  // AND_Gate
  and and_31 (beq, ~in_1[26], ~in_1[27], in_1[28], ~in_1[29], ~in_1[30], ~in_1[31], ins_i_dff40eef);  // AND_Gate
  and and_32 (bnq, in_1[26], ~in_1[27], in_1[28], ~in_1[29], ~in_1[30], ~in_1[31], ins_i_dff40eef);  // AND_Gate
  and and_33 (tty, in_1[0], ~in_1[1], ~in_1[2], R_espec);  // AND_Gate
  and and_34 (\xor , ~in_1[0], ~in_1[1], ~in_1[2], in_1[3], ~in_1[4], in_1[5], R_simple);  // AND_Gate
  and and_35 (OS, ~in_1[0], ~in_1[1], ~in_1[2], in_1[3], ~in_1[4], ~in_1[5], R_simple);  // AND_Gate
  or or_10 (Rrs, blez, bltz, bgtz);
  or or_11 (Mul_Div_1f10744c, div, mult, mulu, divu);
  or or_12 (wrf, and_30_out, andi, ori, xori, slti, lw, sltiu, pop, rnd, kbd, addi);
  and and_36 (mfhi, ~in_1[0], ~in_1[1], ~in_1[2], ~in_1[3], in_1[4], ~in_1[5], R_simple);  // AND_Gate
  and and_37 (mflo, ~in_1[0], in_1[1], ~in_1[2], ~in_1[3], in_1[4], ~in_1[5], R_simple);  // AND_Gate
  and and_38 (blez, ~in_1[26], in_1[27], in_1[28], ~in_1[29], ~in_1[30], ~in_1[31], ins_i_dff40eef);  // AND_Gate
  and and_39 (bgtz, in_1[26], in_1[27], in_1[28], ~in_1[29], ~in_1[30], ~in_1[31], ins_i_dff40eef);  // AND_Gate
  and and_40 (rnd, ~in_1[0], in_1[1], ~in_1[2], R_espec);  // AND_Gate
  or or_13 (Rout, lw, pop);
  Multiplexer #(.select(2), .width(32)) multiplexer_1 (
    .in0({32{1'b0}}), .in1({{17{in_1[15]}}, in_1[14:0]}), .in2({{16{1'b0}}, in_1[15:0]}),
    .in3({{7{in_1[25]}}, in_1[24:0]}), .out(K), .sel(selk));
  Multiplexer #(.width(5)) multiplexer_2 (.in0(in_1[20:16]), .in1(in_1[25:21]), .out(Sb), .sel(Rrs));
  Multiplexer #(.width(5)) multiplexer_3 (.in0(in_1[15:11]), .in1(in_1[20:16]), .out(DA), .sel(ins_i_dff40eef));
  Priority_Encoder priority_encoder_1 (
    .in0(1'b1), .in1(rnd), .in2(Rout), .in3(kbd), .in4(mfhi), .in5(mflo), .out(DS), .en_in(1'b1));  // open: in6, in7, gs, en_out
  or or_14 (Op_const, sltiu, addi, andi, slti, ori, xori);
  Priority_Encoder #(.select(4)) priority_encoder_2 (
    .in0(1'b1), .in1(opsub), .in2(mult), .in3(mulu), .in4(div), .in5(divu), .in6(opand), .in7(opor),
    .in8(opxor), .in9(\nor ), .in10(opslt), .in11(opsltu), .out(Op), .en_in(1'b1));  // open: in12, in13, in14, in15, gs, en_out
  and and_41 (and_41_out, R_simple, ~mflo);  // AND_Gate
  and and_42 (and_42_out, ins_i_dff40eef, ~lw, ~sw);  // AND_Gate
  Priority_Encoder priority_encoder_3 (
    .in0(1'b1), .in1(beq), .in2(bnq), .in3(blez), .in4(bgtz), .in5(bltz), .in6(ins_j_94783cf3), .in7(OS),
    .out(Jump), .en_in(1'b1));  // open: gs, en_out
  Priority_Encoder #(.select(2)) priority_encoder_4 (
    .in0(1'b1), .in1(bltz), .in2(blez), .in3(bgtz), .out(FC), .en_in(1'b1));  // open: gs, en_out
  or or_15 (alu, and_41_out, and_42_out);

  assign Sa = in_1[25:21];

  // Other names for the same wires on the sheet: Const[15:0] = in_1[15:0];
  //   Const1[31:0] = {{17{in_1[15]}}, in_1[14:0]}; Const2[15:0] = in_1[15:0];
  //   const3[31:0] = {{7{in_1[25]}}, in_1[24:0]}; Destino[25:0] = in_1[25:0]; f1 = in_1[0]; funct[5:0] = in_1[5:0];
  //   f2 = in_1[1]; f3 = in_1[2]; f4 = in_1[3]; f5 = in_1[4]; f6 = in_1[5]; jr = OS; muldiv = Mul_Div_1f10744c;
  //   o1 = in_1[26]; Op_code[5:0] = in_1[31:26]; o2 = in_1[27]; o3 = in_1[28]; o4 = in_1[29]; o5 = in_1[30];
  //   o6 = in_1[31]; Rd[4:0] = in_1[15:11]; Rs[4:0] = in_1[25:21]; Rt[4:0] = in_1[20:16]
endmodule

module const_sel (
  input  in_1,
  input  in_2,
  input  in_3,
  output out_4,
  output out_5
);

  wire and_1_out;

  not not_1 (in_2, in_2);
  and and_1 (and_1_out, in_1, in_2);
  or or_1 (out_5, in_3, in_2);
  or or_2 (out_4, in_3, and_1_out);
endmodule
